// Logisim project lab3.circ as structural Verilog: 1 circuit, main circuit main
module main (
  input  b,
  input  a,
  output out_3,
  output out_4
);

  wire and_1_out, and_2_out, and_3_out, and_4_out, CLK_out, not_1_out, not_2_out, or_1_out, or_2_out,
       or_3_out, q0_qn, q1_qn;

  not not_1 (not_1_out, b);
  not not_2 (not_2_out, a);
  and and_1 (and_1_out, out_4, not_1_out);
  and and_2 (and_2_out, q1_qn, b, a);
  and and_3 (and_3_out, out_3, q0_qn, b, not_2_out);
  or or_1 (or_1_out, out_3, not_1_out);
  or or_2 (or_2_out, q1_qn, q0_qn, b);
  or or_3 (or_3_out, and_1_out, and_2_out, and_3_out);
  and and_4 (and_4_out, or_1_out, a, or_2_out);
  Button CLK (.out(CLK_out));
  D_Flip_Flop q1 (.clk(CLK_out), .D(or_3_out), .Q(out_3), .Qn(q1_qn));  // open: preset, en, reset
  D_Flip_Flop q0 (.clk(CLK_out), .D(and_4_out), .Q(out_4), .Qn(q0_qn));  // open: preset, en, reset
endmodule
